# Fritzing sketch noodle (saved by Fritzing 1.0.6)
circuit board: 3.99999cm x 11cm
breadboards: 2

parts:
  100K0 = Rotary Potentiometer (Small) [maximum_resistance=100kΩ knob_status=50% power=0.5W package=THT]
  100K2 = Rotary Potentiometer (Small) [maximum_resistance=100kΩ knob_status=50% power=0.5W package=THT]
  CLK = PJ-301M [part_number=PJ-301M]
  104 = Ceramic Capacitor [capacitance=100nF voltage=16V package="200 mil [THT, multilayer]"]
  rec = PJ-301M [part_number=PJ-301M]
  ][ = PJ-301M [part_number=PJ-301M]
  ~ = PJ-301M [part_number=PJ-301M]
  10k = Resistor [tolerance=±1% resistance=10k power=0.25W package=THT]
  1K = Resistor [tolerance=±5% resistance=1k power=0.25W package=THT]
  103 = Ceramic Capacitor [capacitance=10nF voltage=16V package="200 mil [THT, multilayer]"]
  J3 = shrouded pin header, 16 pins [form="♂ (shrouded male)"]
  100K3 = Rotary Potentiometer (Small) [maximum_resistance=100kΩ knob_status=50% power=0.5W package=THT]
  100K4 = Rotary Potentiometer (Small) [maximum_resistance=100kΩ knob_status=50% power=0.5W package=THT]
  4051B = IC, DIP package, 16 pins [chip_label=4051]
  100uF = Electrolytic Capacitor [capacitance=0.1mF voltage=35V package="100 mil [THT, electrolytic]"]
  40106 = 40106 DIP - 14 pins [chip_label=40106 package="DIP (Dual Inline) [THT]"]
  CD4015 = IC, DIP package, 16 pins [chip_label=4015B]
  5||15 = SPST Switch [package=switch-spdt_kit]
  5817 = Schottky Diode [part_number=1N5817 package="300 mil [THT]"]
  4051B1 = IC, DIP package, 16 pins [chip_label=4051]
  103_2 = Ceramic Capacitor [capacitance=10nF voltage=16V package="200 mil [THT, multilayer]"]
  103_3 = Ceramic Capacitor [capacitance=10nF voltage=16V package="200 mil [THT, multilayer]"]
  rec+ = Pushbutton [package="[THT]"]
  LED2 = LED - 3mm [color="Blue (430nm)" current=0.030A package="3 mm [THT]"]
  1K_2 = Resistor [tolerance=±5% resistance=1k power=0.25W package=THT]
  1K_3 = Resistor [tolerance=±5% resistance=1k power=0.25W package=THT]
  LED1 = LED - 3mm [color="Blue (430nm)" current=0.030A package="3 mm [THT]"]
  LED0 = LED - 3mm [color="Blue (430nm)" current=0.030A package="3 mm [THT]"]
  LED4 = LED - 3mm [color="Blue (430nm)" current=0.030A package="3 mm [THT]"]
  LED6 = LED - 3mm [color="Blue (430nm)" current=0.030A package="3 mm [THT]"]
  1K_4 = Resistor [tolerance=±5% resistance=1k power=0.25W package=THT]
  1K_5 = Resistor [tolerance=±5% resistance=1k power=0.25W package=THT]
  500k = Rotary Potentiometer (Small) [maximum_resistance=500k knob_status=50% power=0.5W package=THT]
  4_7uF = Electrolytic Capacitor [capacitance=4.7µF voltage=35V package="100 mil [THT, electrolytic]"]
  +- = SPST Switch [package=switch-spdt_kit]
  103_4 = Ceramic Capacitor [capacitance=10nF voltage=16V package="200 mil [THT, multilayer]"]
  4_7k = Resistor [tolerance=±1% resistance=4.7k power=0.25W package=THT]
  3_3k = Resistor [tolerance=±1% resistance=3.3k power=0.25W package=THT]
  4_7k_2 = Resistor [tolerance=±5% resistance=1k power=0.25W package=THT]
  3_3k_2 = Resistor [tolerance=±5% resistance=220 power=0.25W package=THT]
  100K1 = Rotary Potentiometer (Small) [maximum_resistance=100kΩ knob_status=50% power=0.5W package=THT]
  5817_2 = Schottky Diode [part_number=1N5817 package="300 mil [THT]"]

nets:
  GND: 100K0.leg1, 100K2.leg1, CLK.Pin_1, 104.0, rec.Pin_1, ][.Pin_1, ~.Pin_1, 103.1, J3.pin2, J3.pin3, J3.pin4, J3.pin13, J3.pin14, J3.pin15, 100K3.leg1, 100K4.leg1, 4051B.pin6, 4051B.pin7, 4051B.pin8, 100uF.-, 40106.pin7, CD4015.pin6, CD4015.pin8, CD4015.pin14, 4051B1.pin6, 4051B1.pin7, 4051B1.pin8, 103_2.1, 103_3.0, LED2.cathode, LED1.cathode, LED0.cathode, LED4.cathode, LED6.cathode, 4_7uF.-, +-.O, 103_4.0, 3_3k.Pin_0, 4_7k_2.Pin_1, 100K1.leg1
  N1: 100K0.wiper, 4051B.pin13
  9V/vdd: 100K0.leg2, 100K2.leg2, 104.1, 103.0, J3.pin5, J3.pin6, J3.pin11, J3.pin12, 100K3.leg2, 100K4.leg2, 4051B.pin16, 100uF.+, 40106.pin14, CD4015.pin16, 4051B1.pin3, 4051B1.pin16, 103_2.0, 103_3.1, +-.S, 103_4.1, 100K1.leg2
  N2: 100K2.wiper, 4051B.pin15
  N3: CLK.Pin_2, 40106.pin2, 500k.leg2
  N4: CLK.Pin_3, 40106.pin11
  N5: rec.Pin_3, 40106.pin13
  N6: ][.Pin_3, 4_7k.Pin_1, 3_3k.Pin_1
  N7: ~.Pin_3, 4_7k_2.Pin_0, 3_3k_2.Pin_1
  N8: 10k.Pin_0, CD4015.pin7, 5||15.P, rec+.Pin_1, rec+.Pin_2
  N9: 10k.Pin_1, CD4015.pin2
  N10: 1K.Pin_0, 4051B1.pin15
  N11: 1K.Pin_1, LED2.anode
  N12: J3.pin1, J3.pin16
  N13: J3.pin7, J3.pin10
  N14: J3.pin8, J3.pin9
  N15: 100K3.wiper, 4051B.pin1, 4051B.pin5
  N16: 100K4.wiper, 4051B.pin2, 4051B.pin4
  N17: 4051B.pin3, 5817.anode
  C: 4051B.pin9, CD4015.pin11, 4051B1.pin9
  B: 4051B.pin10, CD4015.pin4, 4051B1.pin10
  A: 4051B.pin11, CD4015.pin5, 4051B1.pin11
  N18: 4051B.pin12, 4051B.pin14, 100K1.wiper
  N19: 40106.pin1, 500k.leg1, 500k.wiper, 4_7uF.+
  N20: 40106.pin10, CD4015.pin1, CD4015.pin9
  N21: 40106.pin12, 5||15.O
  N22: CD4015.pin3, 5817_2.anode
  N23: CD4015.pin10, CD4015.pin15
  N24: 5817.cathode, 3_3k_2.Pin_0
  N25: 4051B1.pin1, 4051B1.pin5, 1K_4.Pin_1
  N26: 4051B1.pin2, 4051B1.pin4, 1K_5.Pin_1
  N27: 4051B1.pin12, 4051B1.pin14, 1K_2.Pin_0
  N28: 4051B1.pin13, 1K_3.Pin_0
  N29: rec+.Pin_3, rec+.Pin_4, +-.P
  N30: 1K_2.Pin_1, LED1.anode
  N31: 1K_3.Pin_1, LED0.anode
  N32: LED4.anode, 1K_4.Pin_0
  N33: LED6.anode, 1K_5.Pin_0
  N34: 4_7k.Pin_0, 5817_2.cathode

notes:
  noodle
  blueprint@poetaster . de 2026
  jlcjlcjlcjlc

custom parts:
  PJ-301M: Phone power jack.
  40106 DIP - 14 pins: A DIP stand-in part for whatever IC you want. With 14 pins on a 300mil dual inline package (DIP) footprint.
